# Fritzing sketch dogscale breadboard (saved by Fritzing 1.0.1rc)
breadboards: 1

parts:
  Mod1 = Amica NodeMCU DEVKIT 1.0
  S1 = Load Sensor - 50kg [part_number=SEN-10245]
  S2 = Load Sensor - 50kg [part_number=SEN-10245]
  S3 = Load Sensor - 50kg [part_number=SEN-10245]
  S4 = Load Sensor - 50kg [part_number=SEN-10245]
  Bauteil2 = HX711 Weighing Sensor Module MR
  LCD1 = 2.8" SPI TFT Module [part_number=MSP2807]

nets:
  N1: Mod1.pin1, Mod1.pin_10, Mod1.pin_26
  N2: Mod1.pin2, Mod1.pin_9, Mod1.pin_25, Mod1.pin_29, LCD1.pin2
  N3: Mod1.pin5, LCD1.pin3
  N4: Mod1.pin6, LCD1.pin6, LCD1.pin12
  N5: Mod1.pin7, LCD1.pin9, LCD1.pin13
  N6: Mod1.pin8, LCD1.pin7, LCD1.pin10
  N7: Mod1.pin_11, LCD1.pin4
  N8: Mod1.pin_12, LCD1.pin5
  N9: Mod1.pin_15, LCD1.pin11
  N10: S1.B, S2.B
  N11: S1.W, S4.W
  N12: S1.R, Bauteil2.A-
  N13: S2.W, S3.W
  N14: S2.R, Bauteil2.E+
  N15: S3.B, S4.B
  N16: S3.R, Bauteil2.A+
  N17: S4.R, Bauteil2.E-
  N18: LCD1.pin1, LCD1.pin8

custom parts:
  Load Sensor - 50kg: Half-wheatstone bridge Load Cell modified from the Fritzing Repo This load sensor, sometimes called a strain gauge, is the same one found in digital bathroom scales (you know, the ones you use in January for your New Year's resolutions, and then forget about a month later). This sensor can measure up to about 110 pounds.
  HX711 Weighing Sensor Module MR: HX711 is a precision 24-bit analog-to-digital converter (ADC) designed for weigh scales and industrial control applications to interface directly with a bridge sensor.
  2.8" SPI TFT Module: A generic 2.8 inch LCD TFT 320x240 display with touchscreen and SD card slot. Uses the ILI9341 controller, like the Adafruit displays of this size uses.
