# Fritzing sketch dogscale strip board (saved by Fritzing 1.0.1rc)
stripboards: 1
breadboards: 1

parts:
  S1 = Load Sensor - 50kg [part_number=SEN-10245]
  S2 = Load Sensor - 50kg [part_number=SEN-10245]
  S3 = Load Sensor - 50kg [part_number=SEN-10245]
  S4 = Load Sensor - 50kg [part_number=SEN-10245]
  Bauteil2 = HX711 Weighing Sensor Module MR  # not connected
  A1 = SparkFun RJ45 Breakout v11  # not connected
  A2 = SparkFun RJ45 Breakout v11
  LCD2 = 2.8" SPI TFT Module [part_number=MSP2807]
  Mod2 = Amica NodeMCU DEVKIT 1.0

nets:
  N1: S1.B, S2.B
  N2: S1.W, S4.W
  N3: S2.W, S3.W
  N4: S3.B, S4.B
  N5: A2.Pin_3, LCD2.pin2, Mod2.pin2, Mod2.pin_9, Mod2.pin_25, Mod2.pin_29
  N6: A2.Pin_4, Mod2.pin_13
  N7: A2.Pin_5, Mod2.pin_14
  N8: A2.Pin_6, LCD2.pin1, LCD2.pin8
  N9: LCD2.pin3, Mod2.pin5
  N10: LCD2.pin4, Mod2.pin_11
  N11: LCD2.pin5, Mod2.pin_12
  N12: LCD2.pin6, LCD2.pin12, Mod2.pin6
  N13: LCD2.pin7, LCD2.pin10, Mod2.pin8
  N14: LCD2.pin9, LCD2.pin13, Mod2.pin7
  N15: LCD2.pin11, Mod2.pin_15
  N16: Mod2.pin1, Mod2.pin_10, Mod2.pin_26

notes:
  1
  2
  3
  4

custom parts:
  Load Sensor - 50kg: Half-wheatstone bridge Load Cell modified from the Fritzing Repo This load sensor, sometimes called a strain gauge, is the same one found in digital bathroom scales (you know, the ones you use in January for your New Year's resolutions, and then forget about a month later). This sensor can measure up to about 110 pounds.
  HX711 Weighing Sensor Module MR: HX711 is a precision 24-bit analog-to-digital converter (ADC) designed for weigh scales and industrial control applications to interface directly with a bridge sensor.
  SparkFun RJ45 Breakout v11: SparkFun RJ45 Breakout v11 breakout board.
  2.8" SPI TFT Module: A generic 2.8 inch LCD TFT 320x240 display with touchscreen and SD card slot. Uses the ILI9341 controller, like the Adafruit displays of this size uses.
