# Fritzing sketch dogscale (saved by Fritzing 1.0.1rc)
breadboards: 1

parts:
  Mod1 = Amica NodeMCU DEVKIT 1.0
  TFT1 = 1.44" SPI TFT Graphics Display 128x128 - MR 8pin [package=THT]  # not connected
  S1 = Load Sensor - 50kg [part_number=SEN-10245]
  S2 = Load Sensor - 50kg [part_number=SEN-10245]
  S3 = Load Sensor - 50kg [part_number=SEN-10245]
  S4 = Load Sensor - 50kg [part_number=SEN-10245]
  Bauteil2 = HX711 Weighing Sensor Module MR

nets:
  N1: Mod1.pin1, Mod1.pin_10, Bauteil2.VCC
  N2: Mod1.pin2, Mod1.pin_9, Bauteil2.GND
  N3: Mod1.pin_13, Bauteil2.DT
  N4: Mod1.pin_14, Bauteil2.SCK
  N5: S1.B, S2.B
  N6: S1.W, S4.W
  N7: S1.R, Bauteil2.A-
  N8: S2.W, S3.W
  N9: S2.R, Bauteil2.E+
  N10: S3.B, S4.B
  N11: S3.R, Bauteil2.A+
  N12: S4.R, Bauteil2.E-

custom parts:
  Load Sensor - 50kg: Half-wheatstone bridge Load Cell modified from the Fritzing Repo This load sensor, sometimes called a strain gauge, is the same one found in digital bathroom scales (you know, the ones you use in January for your New Year's resolutions, and then forget about a month later). This sensor can measure up to about 110 pounds.
  HX711 Weighing Sensor Module MR: HX711 is a precision 24-bit analog-to-digital converter (ADC) designed for weigh scales and industrial control applications to interface directly with a bridge sensor.
